// Logisim project TP1.circ as structural Verilog: 1 circuit, main circuit main
module main (
  input  in_1,
  input  [3:0] in_2,
  input  [3:0] in_3,
  input  [3:0] in_4,
  input  in_5,
  input  in_6,
  input  [31:0] in_7,
  input  [1:0] in_8
);

  wire [31:0] alu_1_sortie, banc_reg_1_valreg0, banc_reg_1_valreg1, multiplexer_1_out;

  banc_reg banc_reg_1 (
    .clk(in_1), .ValEcriture(alu_1_sortie), .IndReg0(in_2), .IndReg1(in_3), .IndRegEcr(in_4), .SigEcr(in_5),
    .ValReg0(banc_reg_1_valreg0), .Valreg1(banc_reg_1_valreg1));  // open: R15_in
  // Probe on banc_reg_1_valreg1
  Multiplexer #(.width(32)) multiplexer_1 (.in0(banc_reg_1_valreg1), .in1(in_7), .out(multiplexer_1_out), .sel(in_6));
  ALU alu_1 (.Op1(banc_reg_1_valreg0), .Op2(multiplexer_1_out), .Sel(in_8), .Sortie(alu_1_sortie));  // open: NZCV
endmodule
